# Fritzing sketch Circuit (saved by Fritzing 0.9.9b)
breadboards: 1

parts:
  Part1 = Adafruit QT Py ESP32-S2 [part_number="Adafruit #5325"]
  Part2 = Adafruit DRV8833 DC/Stepper Motor Driver [part_number="Adafruit #3297"]
  LED1 = Billie the Blue LED
  LED2 = Ruby the Red LED
  LED3 = Gus the Green LED
  C1 = Cappy the Capacitor
  JACK1 = 2.1mm Barrel Jack with Terminal Block
  S1 = SPST Switch [package=switche-dpdt]
  R1 = Resistor [tolerance=±5% resistance=220 package="0603 [SMD]"]
  R3 = Resistor [tolerance=±5% resistance=220 package="0603 [SMD]"]
  R4 = Resistor [tolerance=±5% resistance=220 package="0603 [SMD]"]
  M1 = DC Motor
  M2 = DC Motor
  R2 = Resistor [tolerance=±5% resistance=220 package="0603 [SMD]"]
  Part3 = Adafruit Micro USB Breakout [part_number="Adafruit #1833"]  # not connected

nets (from the schematic view):
  GND: Part1.GND, Part2.GND, LED1.cathode, LED2.cathode, LED3.cathode, C1.cathode, JACK1.NEG
  N1: Part1.A3, Part1.+5V, C1.anode, S1.O, R3.Pin_0, R4.Pin_0, R2.Pin_0
  N2: Part1.RX, Part2.AIN1
  N3: Part1.SCK, Part2.AIN2
  N4: Part1.MISO, Part2.BIN1
  N5: Part1.MOSI, Part2.BIN2
  N6: Part2.AOUT2, M1.pin_1
  N7: Part2.AOUT1, M1.pin_2
  N8: Part2.BOUT1, M2.pin_1
  N9: Part2.BOUT2, M2.pin_2
  N10: Part2.VMOTOR, Part2.!SLEEP, S1.P
  N11: LED1.anode, LED2.anode, LED3.anode, R1.Pin_1, R3.Pin_1, R4.Pin_1, R2.Pin_1
  N12: JACK1.POS, S1.S

custom parts:
  Adafruit QT Py ESP32-S2: What has your favorite Espressif WiFi microcontroller, comes with our favorite connector - the STEMMA QT, a chainable I2C port, and has lots of Flash and RAM memory for your next IoT project? What will make your next IoT project flyyyyy? What a cutie pie! Or is it... a QT Py? This diminutive dev board comes with one of our new favorite lil chips, the ESP32-S2! The ESP32-S2 is a highly-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
  Adafruit DRV8833 DC/Stepper Motor Driver: Spin two DC motors or step one bi-polar or uni-polar stepper with up to 1.2A per channel using the DRV8833. This motor driver chip is a nice alternative to the TB6612 driver. Like that chip, you get 2 full H-bridges, but this chip is better for low voltage uses (can run from 2.7V up to 10.8V motor power) and has built in current limiting capability. We set it up for 1A current limiting so you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
  Cappy the Capacitor: Cappy E. Lectrifield, a polarized electrolytic capacitor
  Adafruit Micro USB Breakout: Simple but effective - this breakout board has a USB Micro-B connector, with all 5 pins broken out. Great for pairing with a microcontroller with USB support, or adding USB 5V power to a project. We use a micro-AB connector with through-hole shielding pads for an excellent strong connection - it won't rip off by accident! Comes with one fully assembled and tested micro B breakout PCB and a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
